# Fritzing sketch cerberus (saved by Fritzing 0.9.10b)
circuit board: 2.81473cm x 2.54083cm
breadboards: 1

parts:
  R3 = Resistor [tolerance=±5% power=0.25 resistance=1.2 package=THT]
  CON = female pin header, 4 pins [form="♀ (female)"]
  R5 = Resistor [tolerance=±5% power=0.25 resistance=1k package=THT]
  R4 = Resistor [tolerance=±5% power=0.25 resistance=1.2 package=THT]
  R1 = Resistor [tolerance=±5% power=0.25 resistance=1M package=THT]
  R2 = Resistor [tolerance=±5% power=0.25 resistance=150k package=THT]
  WeMos_D1_Mini2 = WeMos D1 Mini
  Out1 = female pin header, 1 pin [form="♀ (female)"]
  IC = female pin header, 1 pin [form="♀ (female)"]
  0V = female pin header, 1 pin [form="♀ (female)"]
  ULN2003A = ULN2003A [package="DIP16 [THT]"]

nets:
  N1: R3.Pin_0, CON.pin1, R4.Pin_0, R1.Pin_1
  N2: R3.Pin_1, R4.Pin_1, Out1.pin1, ULN2003A.Out_1
  N3: CON.pin2, R2.Pin_1, WeMos_D1_Mini2.G, 0V.pin1, ULN2003A.0V
  N4: R5.Pin_0, IC.pin1, ULN2003A.In_1
  N5: R5.Pin_1, WeMos_D1_Mini2.D1
  N6: R1.Pin_0, R2.Pin_0, WeMos_D1_Mini2.D2
